# Fritzing sketch MaglevSwitcher (saved by Fritzing 0.9.3b)
circuit board: 3.38544cm x 3.19405cm
breadboards: 1

parts:
  Q1 = NPN-Transistor [part_number=BD139 package="TO92 [THT]"]
  Q2 = NPN-Transistor [part_number=BD140 package="TO92 [THT]"]
  Q3 = PNP-Transistor [part_number=BD140 package="TO92 [THT]"]
  Q4 = PNP-Transistor [part_number=BD140 package="TO92 [THT]"]
  L1 = Inductor [package="400 mil [THT]"]
  R1 = Resistor [tolerance=±5% resistance=150 package=THT]
  R2 = Resistor [tolerance=±5% resistance=150 package=THT]
  R3 = Resistor [tolerance=±5% resistance=150 package=THT]
  R5 = Resistor [tolerance=±5% resistance=2.2k package=THT]
  Q5 = NPN-Transistor [part_number=2N222A package="TO92 [THT]"]
  U1 = HALL-EFFECT [part_number=TLE4935L package=sc70]
  R6 = Resistor [tolerance=±5% resistance=2.2k package=THT]
  R7 = Resistor [tolerance=±5% resistance=2.2k package=THT]
  R4 = Resistor [tolerance=±5% resistance=150 package=THT]

nets:
  N1: Q1.E, Q3.E, L1.pin_1
  N2: Q1.B, R1.Pin_1
  9V: Q1.C, Q2.C, R5.Pin_1, U1.VCC, R7.Pin_0
  N3: Q2.E, Q4.E, L1.pin_0
  N4: Q2.B, R2.Pin_0
  N5: Q3.B, R3.Pin_1
  GND: Q3.C, Q4.C, R2.Pin_1, Q5.E, U1.GND, R4.Pin_1
  N6: Q4.B, R4.Pin_0
  N7: R1.Pin_0, R3.Pin_0, R5.Pin_0, Q5.C
  N8: Q5.B, R6.Pin_1
  N9: U1.OUT, R6.Pin_0, R7.Pin_1

notes:
  Vcc
  GND
  N. Stathas
